# Fritzing sketch Nodo ProtoBoard (saved by Fritzing 0.9.3b)
breadboards: 1

parts:
  Componente1 = Arduino Pro Mini (5V)
  GY-3 = GY-273 [part_number=GY-273]
  GY1 = MPU-6050 Board GY-521 [form="♀ (female)" package=THT]

nets:
  N1: Componente1.D9, GY-3.SDA, GY1.pin4
  N2: Componente1.D8, GY-3.SCL, GY1.pin3
  N3: GY-3.GND, GY1.pin2
  N4: GY-3.VCC, GY1.pin1

custom parts:
  GY-273: GY-273 - Electronic compass module - 3 Axis Magnetic Field Sensor HMC5883L
  MPU-6050 Board GY-521: Acelerometro y Giroscopio MPU-6050 Board GY-521
